# Fritzing sketch SunRise (saved by Fritzing 0.9.3b)
breadboards: 1

parts:
  Part1 = Arduino Nano (Rev3.0)
  L1 = Inductor [part_number=100мкГн package="400 mil [THT]"]
  D1 = Rectifier Diode [part_number=1N5822 package="300 mil [THT]"]
  C1 = Electrolytic Capacitor [capacitance=470µF voltage=16V package="100 mil [THT, electrolytic]"]
  C2 = Electrolytic Capacitor [capacitance=220µF voltage=25V package="100 mil [THT, electrolytic]"]
  LED1 = LED - 5mm [color="White (6500K)" part_number="10W 12V matrix" package="5 mm [THT]"]
  Q1 = Basic FET N-Channel [part_number=STP16NF06 package="TO220 [THT]"]

nets:
  N1: Part1.GND, C1.-, C2.-, LED1.cathode, Q1.source
  N2: Part1.D3, Q1.gate
  N3: Part1.VIN, L1.pin_0, C1.+
  N4: L1.pin_1, D1.anode, Q1.drain
  N5: D1.cathode, C2.+, LED1.anode
